// Logisim project 实验4 触发器实验.circ as structural Verilog: 6 circuits, main circuit R—S触发器功能测试
module \R_S触发器功能测试  (
  input  Sd,
  input  S,
  input  R,
  input  Rd,
  output Q,
  output nQ
);

  wire clock_1_out;

  Clock #(.highDuration(1), .lowDuration(1)) clock_1 (.out(clock_1_out));
  S_R_Flip_Flop #(.trigger("rising"), .Pre_Clr_Positions("ABOVE_BELOW"), .NegatePresetClear("false"), .enable("false"), .NewFFLayout("true")) s_r_ff_1 (
    .S(S), .clk(clock_1_out), .R(R), .Q(Q), .Qn(nQ), .preset(Sd), .reset(Rd));
endmodule

module \维持_阻塞型D触发器功能测试  (
  input  Sd,
  input  D,
  input  Rd,
  output Q,
  output nQ
);

  wire clock_1_out, not_1_out, not_2_out;

  Clock #(.highDuration(1), .lowDuration(1)) clock_1 (.out(clock_1_out));
  not not_1 (not_1_out, Sd);
  D_Flip_Flop #(.trigger("rising"), .Pre_Clr_Positions("ABOVE_BELOW"), .NegatePresetClear("false"), .enable("false"), .NewFFLayout("true")) d_ff_1 (
    .clk(clock_1_out), .D(D), .Q(Q), .Qn(nQ), .preset(not_1_out), .reset(not_2_out));
  not not_2 (not_2_out, Rd);
  // Digital_Oscilloscope #(.nState(10), .frontlines("rising"), .showclock("true")) digital_oscilloscope_1: pin names not known; wires that end beside it: not_1_out, clock_1_out, D, Q
endmodule

module \负边沿J_K触发器  (
  input  Sd,
  input  J,
  input  K,
  input  Rd,
  output Q,
  output nQ
);

  wire clock_1_out, not_1_out, not_2_out;

  Clock #(.highDuration(1), .lowDuration(1)) clock_1 (.out(clock_1_out));
  not not_1 (not_1_out, Sd);
  not not_2 (not_2_out, Rd);
  J_K_Flip_Flop #(.trigger("rising"), .Pre_Clr_Positions("ABOVE_BELOW"), .NegatePresetClear("false"), .enable("false"), .NewFFLayout("true")) j_k_ff_1 (
    .J(J), .clk(clock_1_out), .K(K), .Q(Q), .Qn(nQ), .preset(not_1_out), .reset(not_2_out));
  // Digital_Oscilloscope #(.nState(10), .frontlines("rising"), .showclock("true")) digital_oscilloscope_1: pin names not known; wires that end beside it: clock_1_out, J, K, Q
endmodule

module \使用D触发器构造一个T触发器  (
  input  T,
  output Q
);

  wire clock_1_out, xor_1_out;

  Clock #(.highDuration(1), .lowDuration(1)) clock_1 (.out(clock_1_out));
  xor xor_1 (xor_1_out, Q, T);
  D_Flip_Flop #(.trigger("rising"), .Pre_Clr_Positions("ABOVE_BELOW"), .NegatePresetClear("false"), .enable("false"), .NewFFLayout("true")) d_ff_1 (
    .clk(clock_1_out), .D(xor_1_out), .Q(Q));  // open: Qn, preset, reset
  // Digital_Oscilloscope #(.nState(10), .frontlines("rising"), .showclock("true")) digital_oscilloscope_1: pin names not known; wires that end beside it: clock_1_out, T, Q
endmodule

module \使用JK触发器构造一个T触发器  (
  input  Sd,
  input  T,
  input  Rd,
  output Q
);

  wire clock_1_out;

  Clock #(.highDuration(1), .lowDuration(1)) clock_1 (.out(clock_1_out));
  J_K_Flip_Flop #(.trigger("rising"), .Pre_Clr_Positions("ABOVE_BELOW"), .NegatePresetClear("false"), .enable("false"), .NewFFLayout("true")) j_k_ff_1 (
    .J(T), .clk(clock_1_out), .K(T), .Q(Q), .preset(Sd), .reset(Rd));  // open: Qn
  // Digital_Oscilloscope #(.nState(10), .frontlines("rising"), .showclock("true")) digital_oscilloscope_1: pin names not known; wires that end beside it: clock_1_out, T, Q
endmodule

module \_4个T_触发器首尾相接  (
  input  Sd,
  input  Rd
);

  wire clock_1_out, t_ff_2_qn, t_ff_3_qn, t_ff_4_qn;
  wire [3:0] t_ff_4_q;

  T_Flip_Flop #(.trigger("rising"), .Pre_Clr_Positions("ABOVE_BELOW"), .NegatePresetClear("false"), .enable("false"), .NewFFLayout("true")) t_ff_1 (
    .clk(t_ff_2_qn), .T(1'b1), .Q(t_ff_4_q[3]), .preset(Sd), .reset(Rd));  // open: Qn
  T_Flip_Flop #(.trigger("rising"), .Pre_Clr_Positions("ABOVE_BELOW"), .NegatePresetClear("false"), .enable("false"), .NewFFLayout("true")) t_ff_2 (
    .clk(t_ff_3_qn), .T(1'b1), .Q(t_ff_4_q[2]), .Qn(t_ff_2_qn), .preset(Sd), .reset(Rd));
  T_Flip_Flop #(.trigger("rising"), .Pre_Clr_Positions("ABOVE_BELOW"), .NegatePresetClear("false"), .enable("false"), .NewFFLayout("true")) t_ff_3 (
    .clk(t_ff_4_qn), .T(1'b1), .Q(t_ff_4_q[1]), .Qn(t_ff_3_qn), .preset(Sd), .reset(Rd));
  T_Flip_Flop #(.trigger("rising"), .Pre_Clr_Positions("ABOVE_BELOW"), .NegatePresetClear("false"), .enable("false"), .NewFFLayout("true")) t_ff_4 (
    .clk(clock_1_out), .T(1'b1), .Q(t_ff_4_q[0]), .Qn(t_ff_4_qn), .preset(Sd), .reset(Rd));
  Clock #(.highDuration(1), .lowDuration(1)) clock_1 (.out(clock_1_out));
  Hex_Digit_Display hex_digit_display_1 (.value(t_ff_4_q));  // open: dp
endmodule
