// Logisim project 实验5  时序逻辑电路 .circ as structural Verilog: 6 circuits, main circuit (1)
module _1 (
  output out_1
);

  wire and_1_out, and_2_out, clock_1_out, j_k_ff_1_q, j_k_ff_2_q, j_k_ff_3_q, j_k_ff_3_qn;

  Clock #(.highDuration(1), .lowDuration(1)) clock_1 (.out(clock_1_out));
  J_K_Flip_Flop #(.trigger("rising"), .Pre_Clr_Positions("ABOVE_BELOW"), .NegatePresetClear("false"), .enable("false"), .NewFFLayout("true")) j_k_ff_1 (
    .J(1'b1), .clk(clock_1_out), .K(1'b1), .Q(j_k_ff_1_q));  // open: Qn, preset, reset
  and and_1 (and_1_out, j_k_ff_3_qn, j_k_ff_1_q);
  J_K_Flip_Flop #(.trigger("rising"), .Pre_Clr_Positions("ABOVE_BELOW"), .NegatePresetClear("false"), .enable("false"), .NewFFLayout("true")) j_k_ff_2 (
    .J(and_1_out), .clk(clock_1_out), .K(j_k_ff_1_q), .Q(j_k_ff_2_q));  // open: Qn, preset, reset
  and and_2 (and_2_out, j_k_ff_1_q, j_k_ff_2_q);
  J_K_Flip_Flop #(.trigger("rising"), .Pre_Clr_Positions("ABOVE_BELOW"), .NegatePresetClear("false"), .enable("false"), .NewFFLayout("true")) j_k_ff_3 (
    .J(and_2_out), .clk(clock_1_out), .K(j_k_ff_1_q), .Q(j_k_ff_3_q), .Qn(j_k_ff_3_qn));  // open: preset, reset
  // Digital_Oscilloscope #(.nState(10), .frontlines("rising"), .showclock("true")) digital_oscilloscope_1: pin names not known; wires that end beside it: and_1_out, clock_1_out, j_k_ff_1_q, j_k_ff_3_q, j_k_ff_2_q
  and and_3 (out_1, j_k_ff_1_q, j_k_ff_3_q);
endmodule

module _2 (
  input  in_1,
  output out_2
);

  wire and_1_out, clock_1_out, j_k_ff_1_q, j_k_ff_2_q, nand_1_out, not_1_out;

  Clock #(.highDuration(1), .lowDuration(1)) clock_1 (.out(clock_1_out));
  nand nand_1 (nand_1_out, in_1, j_k_ff_2_q);
  J_K_Flip_Flop #(.trigger("rising"), .Pre_Clr_Positions("ABOVE_BELOW"), .NegatePresetClear("false"), .enable("false"), .NewFFLayout("true")) j_k_ff_1 (
    .J(in_1), .clk(clock_1_out), .K(nand_1_out), .Q(j_k_ff_1_q));  // open: Qn, preset, reset
  and and_1 (and_1_out, j_k_ff_1_q, in_1);
  not not_1 (not_1_out, in_1);
  J_K_Flip_Flop #(.trigger("rising"), .Pre_Clr_Positions("ABOVE_BELOW"), .NegatePresetClear("false"), .enable("false"), .NewFFLayout("true")) j_k_ff_2 (
    .J(and_1_out), .clk(clock_1_out), .K(not_1_out), .Q(j_k_ff_2_q));  // open: Qn, preset, reset
  // Digital_Oscilloscope #(.nState(10), .frontlines("rising"), .showclock("true")) digital_oscilloscope_1: pin names not known; wires that end beside it: clock_1_out, j_k_ff_2_q, j_k_ff_1_q
  and and_2 (out_2, j_k_ff_1_q, j_k_ff_2_q, in_1);
endmodule

module \_3_串行移位寄存器74LS198  (
  input  [1:0] in_1,
  input  in_2,
  input  [7:0] in_3,
  output [7:0] out_4
);

  wire clock_1_out;

  Clock #(.highDuration(1), .lowDuration(1)) clock_1 (.out(clock_1_out));
  // _74198 74198_1: pin names not known; wires that end beside it: in_1[0], in_3[0], out_4[0], in_3[1], out_4[1], in_3[2], out_4[2], in_3[3], out_4[3], clock_1_out, in_1[1], in_3[7], out_4[7], in_3[6], out_4[6], in_3[5], out_4[5], in_3[4], out_4[4], in_2
  // Digital_Oscilloscope #(.nState(10), .frontlines("rising"), .showclock("true")) digital_oscilloscope_1: pin names not known; wires that end beside it: in_3[0], in_3[1], in_3[2], in_3[3], in_3[4], in_3[5], in_3[6], in_3[7], out_4[0], out_4[1], clock_1_out

  // Other names for the same wires on the sheet: IN[7:0] = in_3; P0 = in_3[0]; P1 = in_3[1]; P2 = in_3[2];
  //   P3 = in_3[3]; P4 = in_3[4]; P5 = in_3[5]; P6 = in_3[6]; P7 = in_3[7]; OUT[7:0] = out_4; Q0 = out_4[0];
  //   Q1 = out_4[1]; Q2 = out_4[2]; Q3 = out_4[3]; Q4 = out_4[4]; Q5 = out_4[5]; Q6 = out_4[6]; Q7 = out_4[7]
endmodule

module \_4__1_74LS198实现环形左移寄存器  (
  input  [1:0] in_1,
  input  in_2,
  input  [7:0] in_3,
  output [7:0] out_4
);

  wire clock_1_out;

  Clock #(.highDuration(1), .lowDuration(1)) clock_1 (.out(clock_1_out));
  // _74198 74198_1: pin names not known; wires that end beside it: in_1[0], out_4[7], in_3[0], out_4[0], in_3[1], out_4[1], in_3[2], out_4[2], in_3[3], out_4[3], clock_1_out, in_1[1], in_3[0], in_3[7], out_4[7], in_3[6], out_4[6], in_3[5], out_4[5], in_3[4], out_4[4], in_2
  // Digital_Oscilloscope #(.nState(10), .frontlines("rising"), .showclock("true")) digital_oscilloscope_1: pin names not known; wires that end beside it: in_3[0], in_3[1], in_3[2], in_3[3], in_3[4], in_3[5], in_3[6], in_3[7], out_4[0], out_4[1], clock_1_out

  // Other names for the same wires on the sheet: IN[7:0] = in_3; P0 = in_3[0]; P1 = in_3[1]; P2 = in_3[2];
  //   P3 = in_3[3]; P4 = in_3[4]; P5 = in_3[5]; P6 = in_3[6]; P7 = in_3[7]; OUT[7:0] = out_4; Q0 = out_4[0];
  //   Q1 = out_4[1]; Q2 = out_4[2]; Q3 = out_4[3]; Q4 = out_4[4]; Q5 = out_4[5]; Q6 = out_4[6]; Q7 = out_4[7]
endmodule

module \_4__2_74LS194实现环形右移寄存器  (
  input  [1:0] in_1,
  input  in_2,
  input  [7:0] in_3,
  output [7:0] out_4
);

  wire clock_1_out;

  Clock #(.highDuration(1), .lowDuration(1)) clock_1 (.out(clock_1_out));
  // _74198 74198_1: pin names not known; wires that end beside it: in_1[0], out_4[0], in_3[0], out_4[0], in_3[1], out_4[1], in_3[2], out_4[2], in_3[3], out_4[3], clock_1_out, in_1[1], out_4[0], in_3[7], out_4[7], in_3[6], out_4[6], in_3[5], out_4[5], in_3[4], out_4[4], in_2
  // Digital_Oscilloscope #(.nState(10), .frontlines("rising"), .showclock("true")) digital_oscilloscope_1: pin names not known; wires that end beside it: in_3[0], in_3[1], in_3[2], in_3[3], in_3[4], in_3[5], in_3[6], in_3[7], out_4[0], out_4[1], clock_1_out

  // Other names for the same wires on the sheet: IN[7:0] = in_3; P0 = in_3[0]; P1 = in_3[1]; P2 = in_3[2];
  //   P3 = in_3[3]; P4 = in_3[4]; P5 = in_3[5]; P6 = in_3[6]; P7 = in_3[7]; OUT[7:0] = out_4; Q0 = out_4[0];
  //   Q1 = out_4[1]; Q2 = out_4[2]; Q3 = out_4[3]; Q4 = out_4[4]; Q5 = out_4[5]; Q6 = out_4[6]; Q7 = out_4[7]
endmodule

module \使用74LS194实现扭环计数器  (
  input  [1:0] in_1,
  input  in_2,
  input  [7:0] in_3,
  output [7:0] out_4
);

  wire clock_1_out, not_1_out;

  not not_1 (not_1_out, out_4[7]);
  Clock #(.highDuration(1), .lowDuration(1)) clock_1 (.out(clock_1_out));
  // _74198 74198_1: pin names not known; wires that end beside it: in_1[1], not_1_out, in_3[0], out_4[0], in_3[1], out_4[1], in_3[2], out_4[2], in_3[3], out_4[3], clock_1_out, in_1[0], out_4[0], in_3[7], out_4[7], in_3[6], out_4[6], in_3[5], out_4[5], in_3[4], out_4[4], in_2
  // Digital_Oscilloscope #(.nState(10), .frontlines("rising"), .showclock("true")) digital_oscilloscope_1: pin names not known; wires that end beside it: in_3[0], in_3[1], in_3[2], in_3[3], in_3[4], in_3[5], in_3[6], in_3[7], out_4[0], out_4[1], clock_1_out

  // Other names for the same wires on the sheet: IN[7:0] = in_3; P0 = in_3[0]; P1 = in_3[1]; P2 = in_3[2];
  //   P3 = in_3[3]; P4 = in_3[4]; P5 = in_3[5]; P6 = in_3[6]; P7 = in_3[7]; OUT[7:0] = out_4; Q0 = out_4[0];
  //   Q1 = out_4[1]; Q2 = out_4[2]; Q3 = out_4[3]; Q4 = out_4[4]; Q5 = out_4[5]; Q6 = out_4[6]; Q7 = out_4[7]
endmodule
