// Logisim project 实验6   计数器实验.circ as structural Verilog: 5 circuits, main circuit 74161
module _74161 (
  input  Reset,
  input  [3:0] in_2,
  input  P,
  input  T,
  input  Load,
  output out_6,
  output [3:0] out_7
);

  wire clock_1_out;

  Clock #(.highDuration(1), .lowDuration(1)) clock_1 (.out(clock_1_out));
  // _74xl00_lib_74161 74161_1: pin names not known; wires that end beside it: Reset, clock_1_out, in_2[0], in_2[1], in_2[2], in_2[3], P, out_6, out_7[0], out_7[1], out_7[2], out_7[3], T, Load, out_7[1], out_7[0], out_7[2]
  Hex_Digit_Display hex_digit_display_1 (.value(out_7));  // open: dp

  // Other names for the same wires on the sheet: D0 = in_2[0]; IN[3:0] = in_2; D1 = in_2[1]; D2 = in_2[2];
  //   D3 = in_2[3]; OUT[3:0] = out_7; Q0 = out_7[0]; Q1 = out_7[1]; Q2 = out_7[2]; Q3 = out_7[3]
endmodule

module \置数法十二进制计数器  (
  input  in_1,
  input  in_2,
  output [3:0] out_3
);

  wire clock_1_out, clock_2_out, n74161_1_p11, n74161_1_p12, n74161_2_p12, n74161_3_p12, nand_3_out,
       or_1_out, or_2_out;
  wire [3:0] ge, shi;

  Clock #(.highDuration(1), .lowDuration(1)) clock_1 (.out(clock_1_out));
  or or_1 (or_1_out, in_1, clock_1_out);
  // _74xl00_lib_74161 74161_1: pin names not known; wires that end beside it: or_1_out, 1'b0, 1'b0, 1'b0, 1'b0, 1'b1, shi[0], shi[1], shi[2], shi[3], n74161_1_p11, n74161_1_p12
  or or_2 (or_2_out, in_2, clock_2_out);
  Clock #(.highDuration(1), .lowDuration(1)) clock_2 (.out(clock_2_out));
  nand nand_1 (n74161_1_p12, shi[0], ge[0]);
  // _74xl00_lib_74161 74161_2: pin names not known; wires that end beside it: or_2_out, 1'b0, 1'b0, 1'b0, 1'b0, 1'b1, out_3[0], out_3[1], out_3[2], out_3[3], 1'b1, n74161_2_p12
  nand nand_2 (n74161_2_p12, out_3[1], out_3[0], out_3[3]);
  // _74xl00_lib_74161 74161_3: pin names not known; wires that end beside it: or_1_out, 1'b0, 1'b0, 1'b0, 1'b0, 1'b1, ge[0], ge[1], ge[2], ge[3], 1'b1, n74161_3_p12
  and and_1 (n74161_3_p12, n74161_1_p12, nand_3_out);
  nand nand_3 (nand_3_out, ge[0], ge[3]);
  and and_2 (n74161_1_p11, ge[0], ge[3]);
  Hex_Digit_Display hex_digit_display_1 (.value(shi));  // open: dp
  Hex_Digit_Display hex_digit_display_2 (.value(ge));  // open: dp
endmodule

module \清零法十二进制计数器  (
  input  in_1,
  input  in_2
);

  wire and_1_out, and_3_out, and_4_out, clock_1_out, clock_2_out, n74161_1_p8, n74161_3_p2, nand_1_out,
       nand_2_out, nand_3_out, or_1_out, or_2_out;
  wire [3:0] ge, n74161_1_p9, shi;

  Clock #(.highDuration(1), .lowDuration(1)) clock_1 (.out(clock_1_out));
  or or_1 (or_1_out, in_1, clock_1_out);
  Clock #(.highDuration(1), .lowDuration(1)) clock_2 (.out(clock_2_out));
  nand nand_1 (nand_1_out, n74161_1_p9[3], n74161_1_p9[2]);
  // _74xl00_lib_74161 74161_1: pin names not known; wires that end beside it: nand_1_out, or_1_out, 1'b0, 1'b0, 1'b0, 1'b0, 1'b1, n74161_1_p8, n74161_1_p9[0], n74161_1_p9[1], n74161_1_p9[2], n74161_1_p9[3], 1'b1, n74161_1_p8
  or or_2 (or_2_out, in_2, clock_2_out);
  nand nand_2 (nand_2_out, ge[1], ge[3]);
  and and_1 (and_1_out, nand_2_out, nand_3_out);
  // _74xl00_lib_74161 74161_2: pin names not known; wires that end beside it: and_1_out, or_2_out, 1'b0, 1'b0, 1'b0, 1'b0, ge[0], ge[1], ge[2], ge[3]
  Hex_Digit_Display hex_digit_display_1 (.value(n74161_1_p9));  // open: dp
  nand nand_3 (nand_3_out, and_3_out, and_4_out);
  // _74xl00_lib_74161 74161_3: pin names not known; wires that end beside it: nand_3_out, n74161_3_p2, 1'b0, 1'b0, 1'b0, 1'b0, shi[0], shi[1], shi[2], shi[3]
  and and_2 (n74161_3_p2, ge[1], ge[3]);
  and and_3 (and_3_out, ge[1], ~ge[0], ~ge[0], ~ge[3]);  // AND_Gate
  and and_4 (and_4_out, shi[0], ~shi[1], ~shi[2], ~shi[3]);  // AND_Gate
  Hex_Digit_Display hex_digit_display_2 (.value(shi));  // open: dp
  Hex_Digit_Display hex_digit_display_3 (.value(ge));  // open: dp
endmodule

module \_74LS161构成一个二进制编码的二十四进制计数器  (
  input  in_1,
  output [7:0] out_2
);

  wire clock_1_out, n74161_1_p12, n74161_1_p13, or_1_out;

  Clock #(.highDuration(1), .lowDuration(1)) clock_1 (.out(clock_1_out));
  or or_1 (or_1_out, in_1, clock_1_out);
  // _74xl00_lib_74161 74161_1: pin names not known; wires that end beside it: 1'b1, or_1_out, 1'b0, 1'b0, 1'b0, 1'b0, 1'b1, out_2[4], out_2[5], out_2[6], out_2[7], n74161_1_p12, n74161_1_p13
  nand nand_1 (n74161_1_p13, out_2[4], out_2[0], out_2[1], out_2[2]);
  // _74xl00_lib_74161 74161_2: pin names not known; wires that end beside it: 1'b1, or_1_out, 1'b0, 1'b0, 1'b0, 1'b0, 1'b1, n74161_1_p12, out_2[0], out_2[1], out_2[2], out_2[3], 1'b1, n74161_1_p13

  // Other names for the same wires on the sheet: t1[3:0] = out_2[7:4]; t2[3:0] = out_2[3:0]
endmodule

module \_74LS161构成一个BCD码二十四进制的计数器  (
);

  wire and_1_out, clock_1_out, n74161_2_p2, nand_1_out, nand_2_out;
  wire [3:0] ge, shi;

  nand nand_1 (nand_1_out, ge[1], ge[3]);
  Clock #(.highDuration(1), .lowDuration(1)) clock_1 (.out(clock_1_out));
  and and_1 (and_1_out, nand_1_out, nand_2_out);
  // _74xl00_lib_74161 74161_1: pin names not known; wires that end beside it: and_1_out, clock_1_out, 1'b0, 1'b0, 1'b0, ge[0], ge[1], ge[2], ge[3]
  nand nand_2 (nand_2_out, ge[2], shi[1]);
  // _74xl00_lib_74161 74161_2: pin names not known; wires that end beside it: nand_2_out, n74161_2_p2, 1'b0, 1'b0, 1'b0, 1'b0, shi[0], shi[1], shi[2], shi[3]
  and and_2 (n74161_2_p2, ge[1], ge[3]);
  Hex_Digit_Display hex_digit_display_1 (.value(ge));  // open: dp
  Hex_Digit_Display hex_digit_display_2 (.value(shi));  // open: dp
endmodule
