// Logisim project 课程设计--发条（电子时钟）.circ as structural Verilog: 14 circuits, main circuit 74161
module _74161 (
  input  Vcc,
  input  nCr,
  input  CP,
  input  D0,
  input  D1,
  input  D2,
  input  D3,
  input  P,
  input  T,
  input  nLd,
  input  GND,
  output Qcc,
  output Q0,
  output Q1,
  output Q2,
  output Q3
);

  wire and_1_out, and_2_out, and_3_out, and_4_out, and_5_out, and_6_out, and_7_out, and_8_out, and_9_out,
       d_ff_1_q, d_ff_1_qn, d_ff_2_q, d_ff_2_qn, d_ff_3_q, d_ff_3_qn, d_ff_4_q, d_ff_4_qn, nand_1_out,
       nand_2_out, nor_1_out, nor_2_out, nor_3_out, nor_4_out, not_1_out, not_2_out, not_3_out, not_4_out,
       not_5_out, or_1_out, or_2_out, or_3_out, or_4_out, or_5_out, xnor_1_out, xnor_2_out, xnor_3_out;

  not not_1 (not_1_out, nLd);
  not not_2 (not_2_out, nCr);
  not not_3 (not_3_out, CP);
  and and_1 (and_1_out, D0, not_1_out);
  not not_4 (not_4_out, not_1_out);
  nand nand_1 (nand_1_out, P, T);
  or or_1 (or_1_out, and_1_out, and_2_out);
  and and_2 (and_2_out, xnor_1_out, not_4_out);
  xnor xnor_1 (xnor_1_out, not_5_out, d_ff_1_qn);
  not not_5 (not_5_out, nand_1_out);
  not not_6 (Q0, d_ff_1_qn);
  D_Flip_Flop #(.trigger("falling"), .Pre_Clr_Positions("BELOW_ABOVE"), .NegatePresetClear("false"), .enable("false"), .NewFFLayout("true")) d_ff_1 (
    .clk(not_3_out), .D(or_1_out), .Q(d_ff_1_q), .Qn(d_ff_1_qn), .reset(not_2_out));  // open: preset
  and and_3 (and_3_out, D1, not_1_out);
  or or_2 (or_2_out, and_3_out, and_4_out);
  and and_4 (and_4_out, xnor_2_out, not_4_out);
  xnor xnor_2 (xnor_2_out, nor_1_out, d_ff_2_qn);
  nor nor_1 (nor_1_out, nand_1_out, d_ff_1_qn);
  not not_7 (Q1, d_ff_2_qn);
  D_Flip_Flop #(.trigger("falling"), .Pre_Clr_Positions("BELOW_ABOVE"), .NegatePresetClear("false"), .enable("false"), .NewFFLayout("true")) d_ff_2 (
    .clk(not_3_out), .D(or_2_out), .Q(d_ff_2_q), .Qn(d_ff_2_qn), .reset(not_2_out));  // open: preset
  or or_3 (or_3_out, and_5_out, and_6_out);
  and and_5 (and_5_out, D2, not_1_out);
  xnor xnor_3 (xnor_3_out, nor_2_out, d_ff_3_qn);
  nor nor_2 (nor_2_out, nand_1_out, d_ff_2_qn, d_ff_1_qn);
  not not_8 (Q2, d_ff_3_qn);
  D_Flip_Flop #(.trigger("falling"), .Pre_Clr_Positions("BELOW_ABOVE"), .NegatePresetClear("false"), .enable("false"), .NewFFLayout("true")) d_ff_3 (
    .clk(not_3_out), .D(or_3_out), .Q(d_ff_3_q), .Qn(d_ff_3_qn), .reset(not_2_out));  // open: preset
  and and_6 (and_6_out, xnor_3_out, not_4_out);
  or or_4 (or_4_out, and_7_out, and_8_out);
  and and_7 (and_7_out, D3, not_1_out);
  and and_8 (and_8_out, not_4_out, or_5_out);
  and and_9 (and_9_out, nor_3_out, d_ff_4_qn);
  nor nor_3 (nor_3_out, nand_1_out, d_ff_3_qn, d_ff_2_qn, d_ff_1_qn);
  not not_9 (Q3, d_ff_4_qn);
  D_Flip_Flop #(.trigger("falling"), .Pre_Clr_Positions("BELOW_ABOVE"), .NegatePresetClear("false"), .enable("false"), .NewFFLayout("true")) d_ff_4 (
    .clk(not_3_out), .D(or_4_out), .Q(d_ff_4_q), .Qn(d_ff_4_qn), .reset(not_2_out));  // open: preset
  or or_5 (or_5_out, and_9_out, nor_4_out);
  nor nor_4 (nor_4_out, nor_3_out, d_ff_4_qn);
  not not_10 (Qcc, nand_2_out);
  nand nand_2 (nand_2_out, d_ff_4_q, d_ff_1_q, d_ff_2_q, d_ff_3_q, T);
endmodule

// 6
module \_6进制计数器  (
  input  Reset,
  input  Enable,
  input  [3:0] CIN,
  input  CP,
  input  Load,
  output [3:0] Q0,
  output CO
);

  wire and_1_out, and_2_out, or_1_out;
  wire [3:0] \二选一数据选择器_四位位二进制数_1_out ;

  \二选一数据选择器_四位位二进制数  \u_二选一数据选择器_四位位二进制数_1  (._0(4'b0000), ._1(CIN), .select(Load), .Out(\二选一数据选择器_四位位二进制数_1_out ));
  and and_1 (and_1_out, Enable, or_1_out);
  or or_1 (or_1_out, Load, and_2_out);
  \十进制计数器  \u_十进制计数器_1  (
    .Reset(Reset), .CIN(\二选一数据选择器_四位位二进制数_1_out ), .Enable(Enable), .Load(and_1_out), .CP(CP), .Q(Q0));  // open: Co
  and and_2 (and_2_out, Q0[2], Q0[0]);
  and and_3 (CO, Q0[2], Q0[0]);
endmodule

// 10
module \十进制计数器  (
  input  Reset,
  input  [3:0] CIN,
  input  Enable,
  input  Load,
  input  CP,
  output [3:0] Q,
  output Co
);

  wire and_1_out, nand_1_out, not_1_out, or_1_out;
  wire [3:0] multiplexer_1_out;

  not not_1 (not_1_out, Reset);
  Multiplexer #(.select(1), .width(4), .disabled("Z"), .enable("false")) multiplexer_1 (
    .in0(4'b0000), .in1(CIN), .out(multiplexer_1_out), .sel(Load));
  _74161 u_74161_1 (
    .nCr(not_1_out), .CP(CP), .D0(multiplexer_1_out[0]), .D1(multiplexer_1_out[1]),
    .D2(multiplexer_1_out[2]), .D3(multiplexer_1_out[3]), .P(Enable), .Q0(Q[0]), .Q1(Q[1]), .Q2(Q[2]),
    .Q3(Q[3]), .T(Enable), .nLd(nand_1_out));  // open: GND, Vcc, Qcc
  nand nand_1 (nand_1_out, Enable, or_1_out);
  or or_1 (or_1_out, Load, and_1_out);
  and and_1 (and_1_out, Q[0], Q[3]);
  and and_2 (Co, Q[0], Q[3]);
endmodule

// 60
module \_60进制计数器  (
  input  [3:0] C1,
  input  [3:0] C0,
  input  Reast,
  input  Enable,
  input  CP,
  input  Load,
  output CO,
  output [3:0] Q0,
  output [3:0] Q1
);

  wire and_1_out, \n6进制计数器_1_co , or_1_out, or_2_out, \十进制计数器_1_co ;
  wire [3:0] \二选一数据选择器_四位位二进制数_1_out , \二选一数据选择器_四位位二进制数_2_out ;

  \二选一数据选择器_四位位二进制数  \u_二选一数据选择器_四位位二进制数_1  (._0(4'b0000), ._1(C0), .select(Load), .Out(\二选一数据选择器_四位位二进制数_1_out ));
  or or_1 (or_1_out, Enable, Load);
  \十进制计数器  \u_十进制计数器_1  (
    .Reset(Reast), .CIN(\二选一数据选择器_四位位二进制数_1_out ), .Enable(or_1_out), .Load(Load), .CP(CP), .Q(Q0),
    .Co(\十进制计数器_1_co ));
  \二选一数据选择器_四位位二进制数  \u_二选一数据选择器_四位位二进制数_2  (._0(4'b0000), ._1(C1), .select(Load), .Out(\二选一数据选择器_四位位二进制数_2_out ));
  or or_2 (or_2_out, Load, and_1_out);
  \_6进制计数器  \u_6进制计数器_1  (
    .Reset(Reast), .Enable(or_2_out), .CIN(\二选一数据选择器_四位位二进制数_2_out ), .CP(CP), .Load(Load), .Q0(Q1),
    .CO(\n6进制计数器_1_co ));
  and and_1 (and_1_out, \十进制计数器_1_co , Enable);
  and and_2 (CO, \n6进制计数器_1_co , \十进制计数器_1_co );
  Hex_Digit_Display hex_digit_display_1 (.value(Q1));  // open: dp
  Hex_Digit_Display hex_digit_display_2 (.value(Q0));  // open: dp
endmodule

// 24
module \_24进制计数器  (
  input  [3:0] C1,
  input  [3:0] C0,
  input  Reset,
  input  Enable,
  input  CP,
  input  Load,
  output [3:0] Q1,
  output [3:0] Q0
);

  wire and_1_out, and_2_out, and_3_out, or_1_out, or_2_out, or_3_out, \十进制计数器_1_co ;
  wire [3:0] \二选一数据选择器_四位位二进制数_1_out , \二选一数据选择器_四位位二进制数_2_out ;

  \二选一数据选择器_四位位二进制数  \u_二选一数据选择器_四位位二进制数_1  (._0(4'b0000), ._1(C0), .select(Load), .Out(\二选一数据选择器_四位位二进制数_1_out ));
  \十进制计数器  \u_十进制计数器_1  (
    .Reset(Reset), .CIN(\二选一数据选择器_四位位二进制数_1_out ), .Enable(or_1_out), .Load(or_2_out), .CP(CP), .Q(Q0),
    .Co(\十进制计数器_1_co ));
  or or_1 (or_1_out, Enable, Load);
  or or_2 (or_2_out, Load, and_3_out);
  \二选一数据选择器_四位位二进制数  \u_二选一数据选择器_四位位二进制数_2  (._0(4'b0000), ._1(C1), .select(Load), .Out(\二选一数据选择器_四位位二进制数_2_out ));
  and and_1 (and_1_out, \十进制计数器_1_co , Enable);
  and and_2 (and_2_out, Enable, Q0[0], Q0[1], Q1[1]);
  \十进制计数器  \u_十进制计数器_2  (
    .Reset(Reset), .CIN(\二选一数据选择器_四位位二进制数_2_out ), .Enable(or_3_out), .Load(or_2_out), .CP(CP), .Q(Q1));  // open: Co
  or or_3 (or_3_out, and_2_out, Load, and_1_out);
  and and_3 (and_3_out, Q1[1], Q0[1], Q0[0]);
  Hex_Digit_Display hex_digit_display_1 (.value(Q1));  // open: dp
  Hex_Digit_Display hex_digit_display_2 (.value(Q0));  // open: dp
endmodule

module \四位数值比较器  (
  input  H1,
  input  H2,
  input  H3,
  input  H4,
  input  nH1,
  input  nH2,
  input  nH3,
  input  nH4,
  output GO
);

  wire and_1_out, and_2_out, and_3_out, and_4_out, and_5_out, and_6_out, and_7_out, and_8_out, nor_1_out,
       nor_2_out, nor_3_out, nor_4_out, not_1_out, not_2_out, not_3_out, not_4_out, not_5_out, not_6_out,
       not_7_out, not_8_out;

  not not_1 (not_1_out, H1);
  not not_2 (not_2_out, nH1);
  not not_3 (not_3_out, H2);
  not not_4 (not_4_out, nH2);
  not not_5 (not_5_out, H3);
  not not_6 (not_6_out, nH3);
  not not_7 (not_7_out, H4);
  not not_8 (not_8_out, nH4);
  and and_1 (and_1_out, not_1_out, nH1);
  and and_2 (and_2_out, not_2_out, H1);
  and and_3 (and_3_out, not_3_out, nH2);
  and and_4 (and_4_out, not_4_out, H2);
  and and_5 (and_5_out, not_5_out, nH3);
  and and_6 (and_6_out, not_6_out, H3);
  and and_7 (and_7_out, not_7_out, nH4);
  and and_8 (and_8_out, not_8_out, H4);
  nor nor_1 (nor_1_out, and_1_out, and_2_out);
  nor nor_2 (nor_2_out, and_3_out, and_4_out);
  nor nor_3 (nor_3_out, and_5_out, and_6_out);
  nor nor_4 (nor_4_out, and_7_out, and_8_out);
  and and_9 (GO, nor_1_out, nor_2_out, nor_3_out, nor_4_out);
endmodule

// 数据比较
module \时钟数值比较器  (
  input  [3:0] H1,
  input  [3:0] nH1,
  input  [3:0] H0,
  input  [3:0] nH0,
  input  [3:0] M1,
  input  [3:0] nM1,
  input  [3:0] M0,
  input  [3:0] nM0,
  output out_9
);

  wire \四位数值比较器_1_go , \四位数值比较器_2_go , \四位数值比较器_3_go , \四位数值比较器_4_go ;

  \四位数值比较器  \u_四位数值比较器_1  (
    .H1(H1[0]), .H2(H1[1]), .H3(H1[2]), .H4(H1[3]), .nH1(nH1[0]), .nH2(nH1[1]), .nH3(nH1[2]), .nH4(nH1[3]),
    .GO(\四位数值比较器_1_go ));
  \四位数值比较器  \u_四位数值比较器_2  (
    .H1(H0[0]), .H2(H0[1]), .H3(H0[2]), .H4(H0[3]), .nH1(nH0[0]), .nH2(nH0[1]), .nH3(nH0[2]), .nH4(nH0[3]),
    .GO(\四位数值比较器_2_go ));
  \四位数值比较器  \u_四位数值比较器_3  (
    .H1(M1[0]), .H2(M1[1]), .H3(M1[2]), .H4(M1[3]), .nH1(nM1[0]), .nH2(nM1[1]), .nH3(nM1[2]), .nH4(nM1[3]),
    .GO(\四位数值比较器_3_go ));
  \四位数值比较器  \u_四位数值比较器_4  (
    .H1(M0[0]), .H2(M0[1]), .H3(M0[2]), .H4(M0[3]), .nH1(nM0[0]), .nH2(nM0[1]), .nH3(nM0[2]), .nH4(nM0[3]),
    .GO(\四位数值比较器_4_go ));
  and and_1 (out_9, \四位数值比较器_1_go , \四位数值比较器_2_go , \四位数值比较器_3_go , \四位数值比较器_4_go );
endmodule

// 24->12
module \进制转换译码器  (
  input  [3:0] in_1,
  input  [3:0] in_2,
  output [3:0] out_3,
  output [3:0] out_4
);

  wire and_1_out, and_2_out, and_3_out, and_4_out, and_5_out, and_6_out, and_7_out, and_8_out, and_9_out,
       and_10_out, and_11_out, and_12_out, not_1_out, not_2_out, not_3_out, not_4_out, not_5_out, not_6_out,
       not_7_out, not_8_out, not_9_out, not_10_out, not_11_out, not_12_out, not_13_out, not_14_out,
       not_15_out, not_16_out;

  not not_1 (not_1_out, in_2[3]);
  not not_2 (not_2_out, in_2[2]);
  not not_3 (not_3_out, in_2[1]);
  not not_4 (not_4_out, in_2[3]);
  not not_5 (not_5_out, in_2[2]);
  not not_6 (not_6_out, in_2[0]);
  not not_7 (not_7_out, in_1[0]);
  not not_8 (not_8_out, in_2[0]);
  not not_9 (not_9_out, in_2[1]);
  not not_10 (not_10_out, in_1[0]);
  not not_11 (not_11_out, in_1[1]);
  not not_12 (not_12_out, in_1[0]);
  not not_13 (not_13_out, in_1[1]);
  not not_14 (not_14_out, in_2[2]);
  not not_15 (not_15_out, in_2[0]);
  not not_16 (not_16_out, in_2[1]);
  and and_1 (and_1_out, in_1[0], not_1_out, not_2_out, not_3_out);
  and and_2 (and_2_out, in_1[0], not_4_out, not_5_out, not_6_out);
  and and_3 (and_3_out, in_1[1], in_2[1]);
  and and_4 (and_4_out, not_7_out, in_2[3], not_8_out);
  or or_1 (out_4[3], and_4_out, and_5_out);
  and and_5 (and_5_out, in_1[1], not_9_out);
  and and_6 (and_6_out, not_10_out, in_2[2]);
  and and_7 (and_7_out, in_2[2], in_2[1]);
  or or_2 (out_4[2], and_6_out, and_7_out, and_8_out);
  and and_8 (and_8_out, in_1[0], in_2[3]);
  and and_9 (and_9_out, not_11_out, not_12_out, in_2[1]);
  and and_10 (and_10_out, not_13_out, not_14_out, in_2[1], not_15_out);
  and and_11 (and_11_out, in_1[0], in_2[2], not_16_out);
  and and_12 (and_12_out, in_1[0], in_2[3]);
  or or_3 (out_3[0], and_1_out, and_2_out, and_3_out);
  or or_4 (out_4[1], and_9_out, and_10_out, and_11_out, and_12_out);

  assign out_3[3:1] = 3'b000;
  assign out_4[0] = in_2[0];
endmodule

// am/pm
module \上午_下午感知器  (
  input  [3:0] in_1,
  input  [3:0] in_2,
  output BOOL
);

  wire and_1_out, and_2_out, and_3_out, and_4_out, not_1_out, not_2_out, not_3_out;

  not not_1 (not_1_out, in_1[0]);
  not not_2 (not_2_out, in_2[3]);
  not not_3 (not_3_out, in_2[2]);
  and and_1 (and_1_out, in_1[0], in_2[1]);
  and and_2 (and_2_out, in_1[0], in_2[2]);
  and and_3 (and_3_out, in_1[0], in_2[3]);
  and and_4 (and_4_out, in_1[1], not_1_out, not_2_out, not_3_out);
  or or_1 (BOOL, and_1_out, and_2_out, and_3_out, and_4_out);

  assign in_1[2] = in_1[3];
endmodule

// 二位选
module \二选一数据选择器_一位二进制数  (
  input  select,
  input  d0,
  input  d1,
  output D
);

  wire and_1_out, and_2_out;

  and and_1 (and_1_out, ~select, d0);  // AND_Gate
  and and_2 (and_2_out, select, d1);
  or or_1 (D, and_1_out, and_2_out);
endmodule

// 四位选
module \二选一数据选择器_四位位二进制数  (
  input  select,
  input  [3:0] _0,
  input  [3:0] _1,
  output [3:0] Out
);

  \二选一数据选择器_一位二进制数  \u_二选一数据选择器_一位二进制数_1  (.d0(_0[0]), .d1(_1[0]), .select(select), .D(Out[0]));
  \二选一数据选择器_一位二进制数  \u_二选一数据选择器_一位二进制数_2  (.d0(_0[1]), .d1(_1[1]), .select(select), .D(Out[1]));
  \二选一数据选择器_一位二进制数  \u_二选一数据选择器_一位二进制数_3  (.d0(_0[2]), .d1(_1[2]), .select(select), .D(Out[2]));
  \二选一数据选择器_一位二进制数  \u_二选一数据选择器_一位二进制数_4  (.d0(_0[3]), .d1(_1[3]), .select(select), .D(Out[3]));
endmodule

// 数码管译码
module \七段数码管译码器  (
  input  a,
  input  c,
  input  b,
  input  d,
  output o1,
  output o2,
  output o3,
  output o4,
  output o5,
  output o6,
  output o7
);

  wire and_1_out, and_2_out, and_3_out, and_4_out, and_5_out, and_6_out, and_7_out, and_8_out, and_9_out,
       and_10_out, and_11_out, and_12_out, and_13_out, and_14_out, and_15_out, and_16_out, and_17_out,
       not_1_out, not_2_out, not_3_out, not_4_out, not_5_out, not_6_out, not_7_out, not_8_out, not_9_out,
       not_10_out, not_11_out, not_12_out, not_13_out, not_14_out, not_15_out, not_16_out, not_17_out,
       not_18_out, not_19_out, not_20_out, not_21_out;

  not not_1 (not_1_out, c);
  and and_1 (and_1_out, not_1_out, not_2_out);
  not not_2 (not_2_out, d);
  and and_2 (and_2_out, c, d);
  not not_3 (not_3_out, c);
  not not_4 (not_4_out, b);
  and and_3 (and_3_out, not_4_out, not_5_out);
  not not_5 (not_5_out, d);
  and and_4 (and_4_out, b, d);
  not not_6 (not_6_out, b);
  or or_1 (o3, not_6_out, d, c);
  not not_7 (not_7_out, c);
  and and_5 (and_5_out, not_7_out, not_8_out);
  not not_8 (not_8_out, d);
  not not_9 (not_9_out, c);
  and and_6 (and_6_out, not_9_out, b);
  and and_7 (and_7_out, b, not_10_out);
  not not_10 (not_10_out, d);
  not not_11 (not_11_out, b);
  and and_8 (and_8_out, c, not_11_out, d);
  not not_12 (not_12_out, c);
  and and_9 (and_9_out, not_12_out, not_13_out);
  not not_13 (not_13_out, d);
  and and_10 (and_10_out, b, not_14_out);
  not not_14 (not_14_out, d);
  and and_11 (and_11_out, a, c);
  not not_15 (not_15_out, b);
  and and_12 (and_12_out, not_15_out, not_16_out);
  not not_16 (not_16_out, d);
  and and_13 (and_13_out, c, not_17_out);
  not not_17 (not_17_out, b);
  and and_14 (and_14_out, c, not_18_out);
  not not_18 (not_18_out, d);
  not not_19 (not_19_out, c);
  and and_15 (and_15_out, not_19_out, b);
  and and_16 (and_16_out, c, not_20_out);
  not not_20 (not_20_out, b);
  and and_17 (and_17_out, c, not_21_out);
  not not_21 (not_21_out, d);
  or or_2 (o1, and_1_out, b, and_2_out, a);
  or or_3 (o2, not_3_out, and_3_out, and_4_out);
  or or_4 (o4, and_5_out, and_6_out, and_7_out, and_8_out, a);
  or or_5 (o5, and_9_out, and_10_out, and_11_out);
  or or_6 (o6, and_12_out, and_13_out, and_14_out, a);
  or or_7 (o7, and_15_out, and_16_out, and_17_out, a);
endmodule

// 发条
module \内部主电路  (
  input  [3:0] Ds1,
  input  [3:0] Ds0,
  input  [3:0] Dm1,
  input  [3:0] Dm0,
  input  [3:0] Dh1,
  input  [3:0] Dh0,
  input  Enable,
  input  Reset,
  input  Load,
  input  Clock,
  input  _12_24,
  input  [3:0] nH1,
  input  [3:0] nH0,
  input  [3:0] nM1,
  input  [3:0] nM0,
  input  ring,
  input  jz,
  input  d,
  input  m,
  output \bool ,
  output compare,
  output [6:0] S1,
  output [6:0] S0,
  output [6:0] M1,
  output [6:0] M0,
  output [6:0] H1,
  output [6:0] H0
);

  wire and_1_out, and_2_out, and_3_out, \n60进制计数器_1_co , \n60进制计数器_2_co , or_1_out, or_2_out,
       \上午_下午感知器_1_bool , \二选一数据选择器_一位二进制数_1_d , \二选一数据选择器_一位二进制数_2_d , \时钟数值比较器_1_out_9 ;
  wire [3:0] \n24进制计数器_1_q0 , \n24进制计数器_1_q1 , \n60进制计数器_1_q0 , \n60进制计数器_1_q1 , \n60进制计数器_2_q0 ,
       \n60进制计数器_2_q1 , \二选一数据选择器_四位位二进制数_1_out , \二选一数据选择器_四位位二进制数_2_out , \进制转换译码器_1_out_3 ,
       \进制转换译码器_1_out_4 ;

  and and_1 (and_1_out, Enable, ~jz);  // AND_Gate
  \_60进制计数器  \u_60进制计数器_1  (
    .Reast(Reset), .Enable(and_1_out), .CP(Clock), .C1(Ds1), .C0(Ds0), .Load(Load), .CO(\n60进制计数器_1_co ),
    .Q0(\n60进制计数器_1_q0 ), .Q1(\n60进制计数器_1_q1 ));
  \七段数码管译码器  \u_七段数码管译码器  (
    .a(\n60进制计数器_1_q1 [3]), .c(\n60进制计数器_1_q1 [2]), .b(\n60进制计数器_1_q1 [1]), .d(\n60进制计数器_1_q1 [0]),
    .o1(S1[0]), .o2(S1[1]), .o3(S1[2]), .o4(S1[3]), .o5(S1[4]), .o6(S1[5]), .o7(S1[6]));
  or or_1 (or_1_out, jz, and_2_out);
  and and_2 (and_2_out, \n60进制计数器_1_co , and_1_out);
  \二选一数据选择器_一位二进制数  \u_二选一数据选择器_一位二进制数_1  (.d0(Clock), .d1(m), .select(jz), .D(\二选一数据选择器_一位二进制数_1_d ));
  \七段数码管译码器  \u_七段数码管译码器_2  (
    .a(\n60进制计数器_1_q0 [3]), .c(\n60进制计数器_1_q0 [2]), .b(\n60进制计数器_1_q0 [1]), .d(\n60进制计数器_1_q0 [0]),
    .o1(S0[0]), .o2(S0[1]), .o3(S0[2]), .o4(S0[3]), .o5(S0[4]), .o6(S0[5]), .o7(S0[6]));
  \_60进制计数器  \u_60进制计数器_2  (
    .Reast(Reset), .Enable(or_1_out), .CP(\二选一数据选择器_一位二进制数_1_d ), .C1(Dm1), .C0(Dm0), .Load(Load),
    .CO(\n60进制计数器_2_co ), .Q0(\n60进制计数器_2_q0 ), .Q1(\n60进制计数器_2_q1 ));
  \七段数码管译码器  \u_七段数码管译码器_3  (
    .a(\n60进制计数器_2_q1 [3]), .c(\n60进制计数器_2_q1 [2]), .b(\n60进制计数器_2_q1 [1]), .d(\n60进制计数器_2_q1 [0]),
    .o1(M1[0]), .o2(M1[1]), .o3(M1[2]), .o4(M1[3]), .o5(M1[4]), .o6(M1[5]), .o7(M1[6]));
  and and_3 (and_3_out, \n60进制计数器_1_co , \n60进制计数器_2_co , and_1_out);
  \_24进制计数器  \u_24进制计数器_1  (
    .Reset(Reset), .Enable(or_2_out), .CP(\二选一数据选择器_一位二进制数_2_d ), .C1(Dh1), .C0(Dh0), .Load(Load),
    .Q1(\n24进制计数器_1_q1 ), .Q0(\n24进制计数器_1_q0 ));
  or or_2 (or_2_out, and_3_out, jz);
  \二选一数据选择器_一位二进制数  \u_二选一数据选择器_一位二进制数_2  (.d0(Clock), .d1(d), .select(jz), .D(\二选一数据选择器_一位二进制数_2_d ));
  \七段数码管译码器  \u_七段数码管译码器_4  (
    .a(\n60进制计数器_2_q0 [3]), .c(\n60进制计数器_2_q0 [2]), .b(\n60进制计数器_2_q0 [1]), .d(\n60进制计数器_2_q0 [0]),
    .o1(M0[0]), .o2(M0[1]), .o3(M0[2]), .o4(M0[3]), .o5(M0[4]), .o6(M0[5]), .o7(M0[6]));
  \进制转换译码器  \u_进制转换译码器_1  (
    .in_1(\n24进制计数器_1_q1 ), .in_2(\n24进制计数器_1_q0 ), .out_3(\进制转换译码器_1_out_3 ), .out_4(\进制转换译码器_1_out_4 ));
  \二选一数据选择器_四位位二进制数  \u_二选一数据选择器_四位位二进制数_1  (
    ._0(\n24进制计数器_1_q1 ), ._1(\进制转换译码器_1_out_3 ), .select(_12_24), .Out(\二选一数据选择器_四位位二进制数_1_out ));
  \七段数码管译码器  \u_七段数码管译码器_5  (
    .a(\二选一数据选择器_四位位二进制数_1_out [3]), .c(\二选一数据选择器_四位位二进制数_1_out [2]), .b(\二选一数据选择器_四位位二进制数_1_out [1]),
    .d(\二选一数据选择器_四位位二进制数_1_out [0]), .o1(H1[0]), .o2(H1[1]), .o3(H1[2]), .o4(H1[3]), .o5(H1[4]), .o6(H1[5]),
    .o7(H1[6]));
  \上午_下午感知器  \u_上午_下午感知器_1  (.in_1(\n24进制计数器_1_q1 ), .in_2(\n24进制计数器_1_q0 ), .BOOL(\上午_下午感知器_1_bool ));
  \二选一数据选择器_四位位二进制数  \u_二选一数据选择器_四位位二进制数_2  (
    ._0(\n24进制计数器_1_q0 ), ._1(\进制转换译码器_1_out_4 ), .select(_12_24), .Out(\二选一数据选择器_四位位二进制数_2_out ));
  \七段数码管译码器  \u_七段数码管译码器_6  (
    .a(\二选一数据选择器_四位位二进制数_2_out [3]), .c(\二选一数据选择器_四位位二进制数_2_out [2]), .b(\二选一数据选择器_四位位二进制数_2_out [1]),
    .d(\二选一数据选择器_四位位二进制数_2_out [0]), .o1(H0[0]), .o2(H0[1]), .o3(H0[2]), .o4(H0[3]), .o5(H0[4]), .o6(H0[5]),
    .o7(H0[6]));
  and and_4 (\bool , \上午_下午感知器_1_bool , _12_24);
  \时钟数值比较器  \u_时钟数值比较器_1  (
    .H1(\n24进制计数器_1_q1 ), .nH1(nH1), .H0(\n24进制计数器_1_q0 ), .nH0(nH0), .M1(\n60进制计数器_2_q1 ), .nM1(nM1),
    .M0(\n60进制计数器_2_q0 ), .nM0(nM0), .out_9(\时钟数值比较器_1_out_9 ));
  and and_5 (compare, Clock, \时钟数值比较器_1_out_9 , ring);
endmodule

module \演示  (
  input  Clock,
  input  ring,
  input  [3:0] nH1,
  input  [3:0] nH0,
  input  [3:0] nM1,
  input  [3:0] nM0,
  input  Load,
  input  [3:0] Dh1,
  input  [3:0] Dh0,
  input  [3:0] Dm1,
  input  [3:0] Dm0,
  input  [3:0] Ds1,
  input  [3:0] Ds0,
  input  Enable,
  input  Reset,
  input  jz,
  input  _12_24
);

  wire Bool, Clock_t, d, m, out;
  wire [6:0] H0, H1, M0, M1, S0, S1;

  \内部主电路  \u_内部主电路_1  (
    .Enable(Enable), .Reset(Reset), .Load(Load), .Clock(Clock_t), ._12_24(_12_24), .Ds1(Ds1), .Ds0(Ds0),
    .Dm1(Dm1), .Dm0(Dm0), .Dh1(Dh1), .Dh0(Dh0), .S1(S1), .S0(S0), .M1(M1), .M0(M0), .jz(jz), .d(d), .m(m),
    .H1(H1), .H0(H0), .\bool (Bool), .nH1(nH1), .nH0(nH0), .compare(out), .nM1(nM1), .nM0(nM0), .ring(ring));
  Clock #(.highDuration(1), .lowDuration(1)) clock_1 (.out(Clock_t));
  Button button_1 (.out(d));
  Button button_2 (.out(m));
  LED #(.active("true")) led_1 (.in(Bool));
  _7_Segment_Display #(.active("true")) u_7_segment_display_1 (
    .g(H0[6]), .f(H0[5]), .a(H0[0]), .b(H0[1]), .e(H0[4]), .d(H0[3]), .c(H0[2]));  // open: dp
  _7_Segment_Display #(.active("true")) u_7_segment_display_2 (
    .g(H1[6]), .f(H1[5]), .a(H1[0]), .b(H1[1]), .e(H1[4]), .d(H1[3]), .c(H1[2]));  // open: dp
  _7_Segment_Display #(.active("true")) u_7_segment_display_3 (
    .g(M1[6]), .f(M1[5]), .a(M1[0]), .b(M1[1]), .e(M1[4]), .d(M1[3]), .c(M1[2]));  // open: dp
  _7_Segment_Display #(.active("true")) u_7_segment_display_4 (
    .g(M0[6]), .f(M0[5]), .a(M0[0]), .b(M0[1]), .e(M0[4]), .d(M0[3]), .c(M0[2]));  // open: dp
  _7_Segment_Display #(.active("true")) u_7_segment_display_5 (
    .g(S1[6]), .f(S1[5]), .a(S1[0]), .b(S1[1]), .e(S1[4]), .d(S1[3]), .c(S1[2]));  // open: dp
  _7_Segment_Display #(.active("true")) u_7_segment_display_6 (
    .g(S0[6]), .f(S0[5]), .a(S0[0]), .b(S0[1]), .e(S0[4]), .d(S0[3]), .c(S0[2]));  // open: dp
  LED #(.active("true")) led_2 (.in(out));

  // Notes on the sheet:
  //   功能控制
  //   输入引脚
  //   :
  //   时钟
  //   :
  //   闹钟
endmodule
